# Fritzing sketch esquema (saved by Fritzing 1.0.1rc)

parts:
  U1 = 2-Channel 5v Relay Shield [package=relay-2ch5v10a]
  V1 = AC Power [voltage=5 frequency=60]  # not connected
  U3 = Transformer [package=transformer]
  J2 = Screw terminal - 2 pins [package=THT]
  J3 = Screw terminal - 2 pins [package=THT]
  JP2 = Header 3 [package=screwterminal-3.5mm-3_lock.007s]
  VALVE1 = Plastic Solenoid Valve
  VALVE2 = Plastic Solenoid Valve
  esp1 = ESP32 DevKitc V4

nets:
  VCC: U1.VCC, esp1.5V
  GND: U1.GND, esp1.GND
  N1: U1.IN1, esp1.IO16
  N2: U1.IN2, esp1.IO17
  N3: U1.K1-In, J2.pin2, VALVE2.no_name_yet#1
  N4: U1.K1-On, U3.3
  N5: U1.K2-In, U1.K2-Off
  N6: U3.1, JP2.3
  N7: U3.2, J2.pin1, VALVE2.no_name_yet#2
  N8: U3.4, JP2.1
  N9: J3.pin1, VALVE1.no_name_yet#2
  N10: J3.pin2, VALVE1.no_name_yet#1

notes:
  Control de riego del huerto, Riego Huerto
  20 V AC
  220 V AC

custom parts:
  2-Channel 5v Relay Shield: 2 Channel 5v Relay Shield w. 2x SPD-06VDC-SD-C
  ESP32 DevKitc V4: ESP32-DevKitC board with ESP32-WROOM-32 module. ESP32-DevKitC V4 is a small-sized ESP32-based development board produced by Espressif. Most of the pins on the ESP module are broken out to the pin headers on the board. The pins D0, D1, D2, D3, CMD and CLK are used internally for communication between ESP32 and SPI flash memory. They are grouped on both sides near the USB connector. Avoid using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
